// Logisim project pipeline.circ as structural Verilog
module FetchUnit (
  input  [7:0] instrORimm,
  input  clk,
  input  reset,
  input  delayIn,
  input  insertNOPE,
  output [7:0] PipelineRegisters,
  output [7:0] nextStage,
  output incPC
);

  wire and_1_out, and_2_out, and_3_out, d_ff_1_q, d_ff_1_qn, nor_1_out, not_1_out, not_2_out, or_1_out;
  wire [1:0] counter_1_q;
  wire [7:0] demultiplexer_1_out0, demultiplexer_1_out1, multiplexer_1_out, multiplexer_2_out, register_1_q,
       register_2_q, register_3_q, register_4_q, register_5_q;

  Multiplexer #(.width(8)) multiplexer_1 (.in0({8{1'b0}}), .in1(instrORimm), .out(multiplexer_1_out), .sel(and_2_out));
  // NoConnect on multiplexer_1_out[0]
  // NoConnect on multiplexer_1_out[1]
  // NoConnect on multiplexer_1_out[2]
  // NoConnect on multiplexer_1_out[3]
  // NoConnect on multiplexer_1_out[4]
  // NoConnect on multiplexer_1_out[5]
  D_Flip_Flop d_ff_1 (.D(nor_1_out), .clk(clk), .Q(d_ff_1_q), .Qn(d_ff_1_qn), .preset(1'b0), .reset(reset));
  Register register_1 (.D(instrORimm), .en(and_2_out), .clk(clk), .Q(register_1_q), .clr(reset));
  not not_1 (not_1_out, delayIn);
  not not_2 (not_2_out, insertNOPE);
  or or_1 (or_1_out, multiplexer_1_out[6], multiplexer_1_out[7]);
  and and_1 (and_1_out, or_1_out, nor_1_out);
  nor nor_1 (nor_1_out, counter_1_q[0], counter_1_q[1]);
  // NoConnect on d_ff_1_qn
  and and_2 (and_2_out, not_1_out, not_2_out);
  Counter #(.max('h3), .ongoal("stay"), .width(2)) counter_1 (
    .load(and_1_out), .D(multiplexer_1_out[7:6]), .count(and_2_out), .Q(counter_1_q), .up(1'b0), .clk(clk),
    .clr(reset));  // open: carry
  Demultiplexer #(.width(8)) demultiplexer_1 (
    .out0(demultiplexer_1_out0), .out1(demultiplexer_1_out1), .in(multiplexer_2_out), .sel(d_ff_1_q));
  Multiplexer #(.width(8)) multiplexer_2 (
    .in0({8{1'b0}}), .in1(register_1_q), .out(multiplexer_2_out), .sel(not_2_out));
  and and_3 (and_3_out, d_ff_1_q, not_1_out);
  Register register_2 (.D(demultiplexer_1_out0), .en(not_1_out), .clk(clk), .Q(register_2_q), .clr(reset));
  Register register_3 (.D(demultiplexer_1_out1), .en(and_3_out), .clk(clk), .Q(register_3_q), .clr(reset));
  Register register_4 (.D(register_2_q), .en(not_1_out), .clk(clk), .Q(register_4_q), .clr(reset));
  Register register_5 (.D(register_3_q), .en(and_3_out), .clk(clk), .Q(register_5_q), .clr(reset));
  Register register_6 (.D(register_4_q), .en(not_1_out), .clk(clk), .Q(PipelineRegisters), .clr(reset));
  Register register_7 (.D(register_5_q), .en(and_3_out), .clk(clk), .Q(nextStage), .clr(reset));
endmodule

module delay (
  input  dIN,
  input  clock,
  input  reset,
  output dOUT,
  output ss
);

  wire d_ff_1_qn, d_ff_2_qn, undriven, undriven_2;

  D_Flip_Flop d_ff_1 (.D(dIN), .clk(clock), .Q(ss), .Qn(d_ff_1_qn), .preset(undriven), .reset(reset));
  // NoConnect on undriven
  D_Flip_Flop d_ff_2 (.D(ss), .clk(clock), .Q(dOUT), .Qn(d_ff_2_qn), .preset(undriven_2), .reset(reset));
  // NoConnect on d_ff_1_qn
  // NoConnect on undriven_2
  // NoConnect on d_ff_2_qn
endmodule

module test (
  input  [7:0] instrORimm,
  input  clk,
  input  reset,
  input  delayIn,
  input  insertNOPE,
  output [7:0] PipelineRegisters,
  output [7:0] nextStage,
  output ready,
  output incPC
);

  wire and_1_out, and_2_out, c, or_1_out, or_2_out, register_1_q, t_ff_1_q, t_ff_1_qn;
  wire [1:0] counter_1_q;
  wire [7:0] demultiplexer_1_out0, demultiplexer_1_out1, multiplexer_1_out, register_2_q, register_3_q,
       register_4_q, register_5_q, register_6_q;

  Multiplexer #(.width(8)) multiplexer_1 (.in0({8{1'b0}}), .in1(instrORimm), .out(multiplexer_1_out), .sel(delayIn));
  // NoConnect on multiplexer_1_out[0]
  // NoConnect on multiplexer_1_out[1]
  // NoConnect on multiplexer_1_out[2]
  // NoConnect on multiplexer_1_out[3]
  // NoConnect on multiplexer_1_out[4]
  // NoConnect on multiplexer_1_out[5]
  Register #(.width(1)) register_1 (.D(c), .en(delayIn), .clk(clk), .Q(register_1_q), .clr(reset));
  or or_1 (or_1_out, delayIn, c);
  // NOT_Gate not_1 has open pins: in=insertNOPE, out=open
  or or_2 (or_2_out, multiplexer_1_out[6], multiplexer_1_out[7]);
  and and_1 (and_1_out, or_2_out, c);
  nor nor_1 (c, counter_1_q[0], counter_1_q[1]);
  Register register_2 (.D(instrORimm), .en(delayIn), .clk(clk), .Q(register_2_q), .clr(reset));
  // NOT_Gate not_2 has open pins: in=t_ff_1_q, out=open
  T_Flip_Flop t_ff_1 (.T(or_1_out), .clk(clk), .Q(t_ff_1_q), .Qn(t_ff_1_qn), .reset(reset), .preset(1'b0));
  // NoConnect on t_ff_1_qn
  Counter #(.max('h3), .ongoal("stay"), .width(2)) counter_1 (
    .load(and_1_out), .D(multiplexer_1_out[7:6]), .count(delayIn), .Q(counter_1_q), .up(1'b0), .clk(clk),
    .clr(reset));  // open: carry
  Demultiplexer #(.width(8)) demultiplexer_1 (
    .out0(demultiplexer_1_out0), .out1(demultiplexer_1_out1), .in(register_2_q), .sel(register_1_q));
  and and_2 (and_2_out, register_1_q, delayIn);
  Register register_3 (.D(demultiplexer_1_out0), .en(delayIn), .clk(clk), .Q(register_3_q), .clr(reset));
  Register register_4 (.D(demultiplexer_1_out1), .en(and_2_out), .clk(clk), .Q(register_4_q), .clr(reset));
  Register register_5 (.D(register_3_q), .en(delayIn), .clk(clk), .Q(register_5_q), .clr(reset));
  Register register_6 (.D(register_4_q), .en(and_2_out), .clk(clk), .Q(register_6_q), .clr(reset));
  Register register_7 (.D(register_5_q), .en(delayIn), .clk(clk), .Q(PipelineRegisters), .clr(reset));
  Register register_8 (.D(register_6_q), .en(and_2_out), .clk(clk), .Q(nextStage), .clr(reset));

  // Notes on the sheet:
  //   delay is used for requesting the pipeline to halt the next cycle 
  //   and it is not meant for handling pipeline hazards
endmodule
